// Logisim project proj.circ as structural Verilog: 4 circuits, main circuit slice
module shift_reg_slice (
  input  SCLKI,
  input  SI,
  input  LDI,
  input  DI,
  output SCLKO,
  output SO,
  output LDO
);

  wire nand_1_out, nand_2_out, nand_3_out, not_1_out;

  not not_1 (not_1_out, LDI);
  nand nand_1 (nand_1_out, SI, LDI);
  nand nand_2 (nand_2_out, not_1_out, DI);
  nand nand_3 (nand_3_out, nand_1_out, nand_2_out);
  D_Flip_Flop d_ff_1 (.clk(SCLKI), .D(nand_3_out), .Q(SO));  // open: Qn, preset, en, reset

  assign LDO = LDI;
  assign SCLKO = SCLKI;
endmodule

module _4_bit_shiftreg (
  input  SI,
  input  LDI,
  input  D0,
  input  D1,
  input  D2,
  input  D3,
  output S0,
  output S1,
  output S2,
  output S3
);

  wire SCLKI_out, shift_reg_slice_1_ldo, shift_reg_slice_1_sclko, shift_reg_slice_2_ldo,
       shift_reg_slice_2_sclko, shift_reg_slice_3_ldo, shift_reg_slice_3_sclko;

  Button SCLKI (.out(SCLKI_out));
  shift_reg_slice shift_reg_slice_1 (
    .SCLKI(SCLKI_out), .SI(SI), .LDI(LDI), .DI(D0), .SCLKO(shift_reg_slice_1_sclko), .SO(S0),
    .LDO(shift_reg_slice_1_ldo));
  shift_reg_slice shift_reg_slice_2 (
    .SCLKI(shift_reg_slice_1_sclko), .SI(S0), .LDI(shift_reg_slice_1_ldo), .DI(D1),
    .SCLKO(shift_reg_slice_2_sclko), .SO(S1), .LDO(shift_reg_slice_2_ldo));
  shift_reg_slice shift_reg_slice_3 (
    .SCLKI(shift_reg_slice_2_sclko), .SI(S1), .LDI(shift_reg_slice_2_ldo), .DI(D2),
    .SCLKO(shift_reg_slice_3_sclko), .SO(S2), .LDO(shift_reg_slice_3_ldo));
  shift_reg_slice shift_reg_slice_4 (
    .SCLKI(shift_reg_slice_3_sclko), .SI(S2), .LDI(shift_reg_slice_3_ldo), .DI(D3), .SO(S3));  // open: SCLKO, LDO

  // Notes on the sheet:
  //   CO
  //   CI
  //   SI
  //   SO
  //   LDI
  //   LDO
  //   D
  //   CO
  //   CI
  //   CI
  //   CO
  //   SI
  //   SO
  //   SI
  //   SO
  //   LDI
  //   LDI
  //   LDO
  //   LDO
  //   D
  //   D
  //   CO
  //   CI
  //   SO
  //   SI
  //   LDI
  //   LDO
  //   D
endmodule

module slice (
  input  CI,
  input  D,
  input  B,
  input  A,
  output F,
  output CO,
  output Q
);

  wire d_ff_1_q, d_ff_2_q, d_ff_3_q, multiplexer_1_out, multiplexer_2_out;

  D_Flip_Flop d_ff_1 (.clk(CI), .D(D), .Q(d_ff_1_q));  // open: Qn, preset, en, reset
  D_Flip_Flop d_ff_2 (.clk(CI), .D(d_ff_1_q), .Q(d_ff_2_q));  // open: Qn, preset, en, reset
  D_Flip_Flop d_ff_3 (.clk(CI), .D(d_ff_2_q), .Q(d_ff_3_q));  // open: Qn, preset, en, reset
  D_Flip_Flop d_ff_4 (.clk(CI), .D(d_ff_3_q), .Q(Q));  // open: Qn, preset, en, reset
  Multiplexer multiplexer_1 (.in0(d_ff_1_q), .in1(d_ff_2_q), .out(multiplexer_1_out), .sel(A));  // open: en
  Multiplexer multiplexer_2 (.in0(d_ff_3_q), .in1(Q), .out(multiplexer_2_out), .sel(A));  // open: en
  Multiplexer multiplexer_3 (.in0(multiplexer_1_out), .in1(multiplexer_2_out), .out(F), .sel(B));  // open: en

  assign CO = CI;
endmodule

module top (
  input  Config,
  input  P,
  output F,
  output Q
);

  wire CI_2_out, CI_out, d_ff_1_q, d_ff_2_q, d_ff_3_q, d_ff_4_q, d_ff_5_q, d_ff_6_q, d_ff_7_q, d_ff_8_q,
       slice_1_co, slice_1_f, slice_1_q, slice_2_co, slice_2_f, slice_2_q, slice_4_co, slice_4_f, slice_4_q,
       slice_5_co, slice_5_f, slice_5_q, slice_6_co, slice_6_f, slice_6_q, slice_7_co, slice_7_f, slice_7_q;

  D_Flip_Flop d_ff_1 (.clk(CI_out), .D(P), .Q(d_ff_1_q));  // open: Qn, preset, en, reset
  Button CI (.out(CI_out));
  Button CI_2 (.out(CI_2_out));
  D_Flip_Flop d_ff_2 (.clk(CI_out), .D(d_ff_1_q), .Q(d_ff_2_q));  // open: Qn, preset, en, reset
  slice slice_1 (
    .CI(slice_7_co), .D(slice_7_q), .B(slice_4_f), .A(slice_2_f), .F(slice_1_f), .CO(slice_1_co),
    .Q(slice_1_q));
  slice slice_2 (.CI(CI_2_out), .D(Config), .B(d_ff_2_q), .A(d_ff_1_q), .F(slice_2_f), .CO(slice_2_co), .Q(slice_2_q));
  D_Flip_Flop d_ff_3 (.clk(CI_out), .D(d_ff_2_q), .Q(d_ff_3_q));  // open: Qn, preset, en, reset
  slice slice_3 (.CI(slice_5_co), .D(slice_5_q), .B(slice_5_f), .A(slice_1_f), .F(F), .Q(Q));  // open: CO
  slice slice_4 (
    .CI(slice_2_co), .D(slice_2_q), .B(d_ff_4_q), .A(d_ff_3_q), .F(slice_4_f), .CO(slice_4_co), .Q(slice_4_q));
  D_Flip_Flop d_ff_4 (.clk(CI_out), .D(d_ff_3_q), .Q(d_ff_4_q));  // open: Qn, preset, en, reset
  slice slice_5 (
    .CI(slice_1_co), .D(slice_1_q), .B(slice_7_f), .A(slice_6_f), .F(slice_5_f), .CO(slice_5_co),
    .Q(slice_5_q));
  slice slice_6 (
    .CI(slice_4_co), .D(slice_4_q), .B(d_ff_6_q), .A(d_ff_5_q), .F(slice_6_f), .CO(slice_6_co), .Q(slice_6_q));
  slice slice_7 (
    .CI(slice_6_co), .D(slice_6_q), .B(d_ff_8_q), .A(d_ff_7_q), .F(slice_7_f), .CO(slice_7_co), .Q(slice_7_q));
  D_Flip_Flop d_ff_5 (.clk(CI_out), .D(d_ff_4_q), .Q(d_ff_5_q));  // open: Qn, preset, en, reset
  D_Flip_Flop d_ff_6 (.clk(CI_out), .D(d_ff_5_q), .Q(d_ff_6_q));  // open: Qn, preset, en, reset
  D_Flip_Flop d_ff_7 (.clk(CI_out), .D(d_ff_6_q), .Q(d_ff_7_q));  // open: Qn, preset, en, reset
  D_Flip_Flop d_ff_8 (.clk(CI_out), .D(d_ff_7_q), .Q(d_ff_8_q));  // open: Qn, preset, en, reset
endmodule
